# Fritzing sketch Untitled Sketch (saved by Fritzing 0.9.3b)
circuit board: 15.0437cm x 8.3108cm

parts:
  Componente1 = Arduino Mega ADK (Rev3)
  KY-1 = Keyes Relay [package=THT]
  Componente2 = Bluetooth HC-05 Macho

nets:
  GND: Componente1.GND, KY-1.ground, Componente2.GND
  5V: Componente1.5V, KY-1.power, Componente2.VCC
  N1: Componente1.D0/RX0, Componente2.TXD
  N2: Componente1.D1/TX0, Componente2.RXD
  N3: Componente1.D5_PWM, KY-1.signal

notes:
  Relay / Bluetooth

custom parts:
  Keyes Relay: The Keyes 5V relay module is suitable for SCM development, home appliance control. It uses a 5V~12V TIL control signal which can control DC / AC signal.
